# Fritzing sketch basic_schematic (saved by Fritzing 0.9.3b)
breadboards: 1

parts:
  part = Arduino Pro Mini v13
  SI48735 = IC, DIP package, 24 pins [chip_label=IC]
  L1 = Inductor [package="400 mil [THT]"]
  C3 = Capacitor [part_number=470nF package=cap-pth-large]
  C2 = Capacitor [part_number=1nF package=cap-pth-small2]
  FM_Antenna = Antenna
  C1 = Capacitor [part_number=22nF package=cap-pth-large]
  X1 = CRYSTAL [package=crystal-32khz-smd_epson_mc146]
  R3 = Resistor [tolerance=±5% resistance=2.2k package="0402 [SMD]"]
  R4 = Resistor [tolerance=±5% resistance=10k package="0402 [SMD]"]
  R5 = Resistor [tolerance=±5% resistance=10k package="0402 [SMD]"]

nets:
  N1: part.A4, SI48735.pin18, R4.Pin_1
  N2: part.A5, SI48735.pin17, R5.Pin_0
  GND: part.GND, SI48735.pin10, SI48735.pin13, SI48735.pin16
  3.3V: part.VCC, SI48735.pin20, SI48735.pin21, R4.Pin_0, R5.Pin_1
  N3: part.D12/MISO, SI48735.pin15
  N4: part.D2, SI48735.pin4
  N5: SI48735.pin3, R3.Pin_1
  N6: SI48735.pin8, C2.2
  N7: SI48735.pin9, L1.pin_1
  N8: SI48735.pin12, C3.1
  N9: SI48735.pin19, X1.2
  N10: SI48735.pin22, C1.1
  N11: L1.pin_0, C3.2
  N12: C2.1, FM_Antenna.antenna_lead
  N13: X1.1, R3.Pin_0

notes:
  SI4735 - Minimal Schematic
  Ricardo Lima Caratti - Nov 2019
  SLC
  SDA
  SI4844 Pin 2 (Interrupt)
  RESET (RST)
